// Logisim project exerc1.circ as structural Verilog: 1 circuit, main circuit main
module main (
);

  wire button_1_out, nand_1_out, nand_2_out, not_1_out, not_2_out, s_r_ff_1_q, s_r_ff_1_qn;

  nand nand_1 (nand_1_out, s_r_ff_1_qn, not_1_out);
  not not_1 (not_1_out, 1'b0);
  not not_2 (not_2_out, 1'b0);
  nand nand_2 (nand_2_out, not_2_out, s_r_ff_1_q);
  Random #(.width(2)) random_1 ();  // open: clk, next, out, clr
  Button button_1 (.out(button_1_out));
  S_R_Flip_Flop #(.trigger("low")) s_r_ff_1 (
    .S(nand_1_out), .clk(button_1_out), .R(nand_2_out), .Q(s_r_ff_1_q), .Qn(s_r_ff_1_qn), .en(1'b1));  // open: preset, reset
  LED led_1 (.in(s_r_ff_1_q));
  LED led_2 (.in(s_r_ff_1_qn));
endmodule
