// Logisim project exerc2a.circ as structural Verilog: 1 circuit, main circuit main
module main (
);

  wire Clear_out, CLK_out, d_ff_1_q, d_ff_2_q, d_ff_3_q, d_ff_4_q;

  Button CLK (.out(CLK_out));
  Button Clear (.out(Clear_out));
  D_Flip_Flop #(.trigger("falling")) d_ff_1 (
    .clk(CLK_out), .D(1'b1), .Q(d_ff_1_q), .preset(1'b1), .en(1'b1), .reset(Clear_out));  // open: Qn
  LED led_1 (.in(d_ff_1_q));
  D_Flip_Flop #(.trigger("falling")) d_ff_2 (
    .clk(CLK_out), .D(1'b1), .Q(d_ff_2_q), .preset(1'b1), .en(1'b1), .reset(Clear_out));  // open: Qn
  D_Flip_Flop #(.trigger("falling")) d_ff_3 (
    .clk(CLK_out), .D(1'b0), .Q(d_ff_3_q), .preset(1'b1), .en(1'b1), .reset(Clear_out));  // open: Qn
  LED led_2 (.in(d_ff_2_q));
  LED led_3 (.in(d_ff_3_q));
  D_Flip_Flop #(.trigger("falling")) d_ff_4 (
    .clk(CLK_out), .D(1'b1), .Q(d_ff_4_q), .preset(1'b1), .en(1'b1), .reset(Clear_out));  // open: Qn
  LED led_4 (.in(d_ff_4_q));
endmodule
