// Logisim project exerc4.circ as structural Verilog: 1 circuit, main circuit main
module main (
);

  wire clock_1_out, j_k_ff_1_qn, j_k_ff_2_qn, j_k_ff_3_qn, j_k_ff_4_qn;
  wire [1:0] j_k_ff_2_q;

  Clock clock_1 (.out(clock_1_out));
  J_K_Flip_Flop #(.trigger("falling")) j_k_ff_1 (
    .J(j_k_ff_2_q[0]), .clk(clock_1_out), .K(j_k_ff_3_qn), .Q(j_k_ff_2_q[1]), .Qn(j_k_ff_1_qn), .en(1'b1));  // open: preset, reset
  J_K_Flip_Flop #(.trigger("falling")) j_k_ff_2 (
    .J(j_k_ff_2_q[1]), .clk(clock_1_out), .K(j_k_ff_1_qn), .Q(j_k_ff_2_q[0]), .Qn(j_k_ff_2_qn), .en(1'b1));  // open: preset, reset
  J_K_Flip_Flop #(.trigger("falling")) j_k_ff_3 (
    .J(j_k_ff_2_q[0]), .clk(clock_1_out), .K(j_k_ff_4_qn), .Q(j_k_ff_2_q[0]), .Qn(j_k_ff_3_qn), .en(1'b1));  // open: preset, reset
  J_K_Flip_Flop #(.trigger("falling")) j_k_ff_4 (
    .J(j_k_ff_2_q[0]), .clk(clock_1_out), .K(j_k_ff_2_qn), .Q(j_k_ff_2_q[0]), .Qn(j_k_ff_4_qn), .en(1'b1));  // open: preset, reset
endmodule
